# Fritzing sketch sketch (saved by Fritzing 1.0.4)
circuit board: 15.3463cm x 9.82233cm
breadboards: 1

parts:
  M2 = DC Motor [voltage_(max)=5V voltage_(min)=3V]
  A1 = Esp32-c3 super mini
  S2 = Pushbutton [package="[THT]"]
  S3 = Pushbutton [package="[THT]"]
  S4 = Pushbutton [package="[THT]"]
  S5 = Pushbutton [package="[THT]"]
  S6 = Pushbutton [package="[THT]"]
  S7 = Pushbutton [package="[THT]"]
  S8 = Pushbutton [package="[THT]"]
  S1 = Pushbutton [package="[THT]"]
  Power_plug1 = Power plug
  M3 = DC Motor [voltage_(max)=5V voltage_(min)=3V]
  M4 = DC Motor [voltage_(max)=5V voltage_(min)=3V]
  M5 = DC Motor [voltage_(max)=5V voltage_(min)=3V]
  Bauteil2 = VL530X Time of Flight Distance Sensor [part_number="tonetoys #3317"]
  Q1 = Basic FET N-Channel [package="TO220 [THT]"]
  Q2 = Basic FET N-Channel [package="TO220 [THT]"]
  Q3 = Basic FET N-Channel [package="TO220 [THT]"]
  Q4 = Basic FET N-Channel [package="TO220 [THT]"]
  M1 = Arduino Nano (Rev3.0)
  R1 = Resistor [tolerance=±5% power=0.25W resistance=1k package=THT]
  R2 = Resistor [tolerance=±5% power=0.25W resistance=1.5k package=THT]
  D1 = Schottky Diode [part_number=1N5819 package="300 mil [THT]"]
  D2 = Schottky Diode [part_number=1N5819 package="300 mil [THT]"]
  D3 = Schottky Diode [part_number=1N5819 package="300 mil [THT]"]
  D4 = Schottky Diode [part_number=1N5819 package="300 mil [THT]"]
  J1 = Piezo Speaker

nets:
  VCC: M2.pin_1, A1.Pin_16, Power_plug1.VCC, M3.pin_1, M4.pin_1, M5.pin_1, M1.VIN, D1.cathode, D2.cathode, D3.cathode, D4.cathode
  N1: M2.pin_2, Q4.drain, D4.anode
  N2: A1.Pin_4, S6.Pin_4
  N3: A1.Pin_5, S7.Pin_3, S7.Pin_4
  N4: A1.Pin_6, S8.Pin_3, S8.Pin_4
  N5: A1.Pin_7, R1.Pin_1, R2.Pin_0
  N6: A1.Pin_8, M1.D0/RX
  N7: A1.Pin_9, S5.Pin_4
  N8: A1.Pin_10, S4.Pin_3, S4.Pin_4
  N9: A1.Pin_11, S3.Pin_3, S3.Pin_4
  N10: A1.Pin_12, S2.Pin_3, S2.Pin_4
  N11: A1.Pin_13, S1.Pin_3, S1.Pin_4
  N12: A1.Pin_14, S2.Pin_1, S2.Pin_2, S3.Pin_1, S3.Pin_2, S4.Pin_1, S4.Pin_2, S5.Pin_1, S5.Pin_2, S6.Pin_1, S6.Pin_2, S7.Pin_1, S7.Pin_2, S8.Pin_1, S8.Pin_2, S1.Pin_1, S1.Pin_2
  GND: A1.Pin_15, Power_plug1.GND, Bauteil2.GND, Q1.source, Q2.source, Q3.source, Q4.source, M1.GND, R2.Pin_1, J1.pin1
  N13: M3.pin_2, Q3.drain, D3.anode
  N14: M4.pin_2, Q2.drain, D2.anode
  N15: M5.pin_2, Q1.drain, D1.anode
  VCC_2: Bauteil2.VCC, M1.3V3
  N16: Bauteil2.SCL, M1.A5
  N17: Bauteil2.SDA, M1.A4
  N18: Q1.gate, M1.D2
  N19: Q2.gate, M1.D3
  N20: Q3.gate, M1.D4
  N21: Q4.gate, M1.D5
  N22: M1.D1/TX, R1.Pin_0
  N23: M1.D10, J1.pin2

notes:
  5V

custom parts:
  Esp32-c3 super mini: ESP32-C3 Development Board ESP32 SuperMini Development Board ESP32 Development Board WiFi Bluetooth.
  VL530X Time of Flight Distance Sensor: TOF
